# Fritzing sketch Backpack of Awesome-common anode (saved by Fritzing 0.8.7b)

parts:
  LED1 = RGB LED (com. anode, rbg) [package="5 mm [THT]"]
  S1 = Pushbutton [part_number="Status Button" package=THT]
  S2 = Pushbutton [part_number="Video Button" package=THT]
  S3 = Pushbutton [part_number="Audio Button" package=THT]
  Raspberry_Pi_B_rev1 = Raspberry Pi B rev2
  R1 = Resistor [tolerance=±5% resistance=470 package=THT]
  R2 = Resistor [tolerance=±5% resistance=470 package=THT]
  R3 = Resistor [tolerance=±5% resistance=1k package=THT]
  U1 = mystery part, 9 pins [chip_label=GPS part_number="Ultimate GPS Breakout v3"]
  J1 = female pin header, 3 pins [form="♀ (female)"]

nets:
  N1: LED1.red_cathode, R3.Pin_0
  N2: LED1.common_anode, S1.leg0
  N3: LED1.blue_cathode, R2.Pin_0
  N4: LED1.green_cathode, R1.Pin_0
  N5: S1.leg1, Raspberry_Pi_B_rev1.3V3, J1.pin1
  N6: S2.leg0, S3.leg0, J1.pin2
  N7: S2.leg1, Raspberry_Pi_B_rev1.GPIO_17
  N8: S3.leg1, Raspberry_Pi_B_rev1.GPIO_18
  N9: Raspberry_Pi_B_rev1.5V, U1.pin8
  N10: Raspberry_Pi_B_rev1.GND, U1.pin7
  N11: Raspberry_Pi_B_rev1.GPIO_23, R2.Pin_1
  N12: Raspberry_Pi_B_rev1.GPIO_14, U1.pin6
  N13: Raspberry_Pi_B_rev1.GPIO_15, U1.pin5
  N14: Raspberry_Pi_B_rev1.GPIO_22, R3.Pin_1
  N15: Raspberry_Pi_B_rev1.GPIO_24, R1.Pin_1
  N16: U1.pin1, U1.pin2
